# Fritzing sketch Automacao APM (saved by Fritzing 0.9.3b)
circuit board: 12.09cm x 2.08cm
breadboards: 1

parts:
  DISPLAY = LCD-16X2 [package=lcd-16x2_noholes]
  R1-DIS = Resistor [tolerance=±5% resistance=220 package=THT]
  S-TEMP = Temperature Sensor (Thermistor) [thermistor_type=NTC package=THT]
  R2-TEMP = Resistor [tolerance=±5% resistance=10k package=THT]
  IR-OUT = LED - 3mm [color="Infrared (880nm)" package="3 mm [THT]"]
  R3-IROUT = Resistor [tolerance=±5% resistance=220 package=THT]
  M-RELE = Keyes Relay [package=THT]
  IR-IN = TSOP312.., 314.. [package=THT]
  Arduino1 = Arduino Mini (Rev5)

nets:
  GND: DISPLAY.VSS, DISPLAY.VO, DISPLAY.R_W, DISPLAY.K, S-TEMP.pin_0, R2-TEMP.Pin_0, R2-TEMP.Pin_1, IR-OUT.anode, M-RELE.ground, IR-IN.GND, Arduino1.A0, Arduino1.GND
  VDD: DISPLAY.VDD, R1-DIS.Pin_0, S-TEMP.pin_1, M-RELE.power, IR-IN.Vs, Arduino1.5V
  N1: DISPLAY.RS, Arduino1.D2
  N2: DISPLAY.E, Arduino1.D4
  N3: DISPLAY.DB4, Arduino1.D5_PWM
  N4: DISPLAY.DB5, Arduino1.D6_PWM
  N5: DISPLAY.DB6, Arduino1.D7
  N6: DISPLAY.DB7, Arduino1.D8
  N7: DISPLAY.A, R1-DIS.Pin_1
  N8: IR-OUT.cathode, R3-IROUT.Pin_1
  N9: R3-IROUT.Pin_0, Arduino1.D3_PWM
  N10: M-RELE.signal, Arduino1.D12
  N11: IR-IN.Data, Arduino1.D11_PWM

custom parts:
  Keyes Relay: The Keyes 5V relay module is suitable for SCM development, home appliance control. It uses a 5V~12V TIL control signal which can control DC / AC signal.
